// Logisim project projeto.circ as structural Verilog: 9 circuits, main circuit comparador 1
module comparador_1 (
  input  in_1,
  input  in_2,
  output out_3
);

  wire and_1_out, and_2_out, not_1_out, not_2_out;

  not not_1 (not_1_out, in_1);
  not not_2 (not_2_out, in_2);
  and and_1 (and_1_out, not_1_out, not_2_out);
  and and_2 (and_2_out, in_2, in_1);
  or or_1 (out_3, and_1_out, and_2_out);
endmodule

module comparador_4 (
  input  [3:0] in_1,
  input  [3:0] in_2,
  output out_3
);

  wire and_1_out, and_2_out, comparador_1_1_out_3, comparador_1_2_out_3, comparador_1_3_out_3,
       comparador_1_4_out_3;

  comparador_1 comparador_1_1 (.in_1(in_1[0]), .in_2(in_2[0]), .out_3(comparador_1_1_out_3));
  comparador_1 comparador_1_2 (.in_1(in_1[1]), .in_2(in_2[1]), .out_3(comparador_1_2_out_3));
  comparador_1 comparador_1_3 (.in_1(in_1[2]), .in_2(in_2[2]), .out_3(comparador_1_3_out_3));
  comparador_1 comparador_1_4 (.in_1(in_1[3]), .in_2(in_2[3]), .out_3(comparador_1_4_out_3));
  and and_1 (and_1_out, comparador_1_1_out_3, comparador_1_2_out_3);
  and and_2 (and_2_out, comparador_1_3_out_3, comparador_1_4_out_3);
  and and_3 (out_3, and_1_out, and_2_out);
endmodule

module Guess (
  input  confirmar,
  input  novo,
  input  [3:0] chute,
  output [7:0] Red,
  output [7:0] Blue,
  output out_6
);

  wire comparador_out_3, not_1_out;
  wire [3:0] \diferença_out_3 , random_1_out, subtrator_4_1_out_3;
  wire [7:0] bit_extender_1_out, bit_extender_2_out, leftshift_4_1_out_2, leftshift_4_2_out_2;

  Random #(.width(4)) random_1 (.clk(novo), .out(random_1_out));  // open: next, clr
  assign bit_extender_1_out = {{7{confirmar}}, confirmar};  // Bit_Extender bit_extender_1
  \diferença  \diferença  (.in_1(random_1_out), .in_2(chute), .out_3(\diferença_out_3 ));
  not not_1 (not_1_out, comparador_out_3);
  comparador_4 comparador (.in_1(random_1_out), .in_2(chute), .out_3(comparador_out_3));
  assign bit_extender_2_out = {{7{not_1_out}}, not_1_out};  // Bit_Extender bit_extender_2
  assign Red = bit_extender_1_out & bit_extender_2_out & leftshift_4_1_out_2;  // AND_Gate and_1, 8 bits wide
  leftshift_4 leftshift_4_1 (.out_2(leftshift_4_1_out_2), .in_1(\diferença_out_3 ));
  subtrator_4 subtrator_4_1 (.x(4'b1111), .y(\diferença_out_3 ), .out_3(subtrator_4_1_out_3));  // open: out_4
  leftshift_4 leftshift_4_2 (.out_2(leftshift_4_2_out_2), .in_1(subtrator_4_1_out_3));
  assign Blue = leftshift_4_2_out_2 & bit_extender_2_out & bit_extender_1_out;  // AND_Gate and_2, 8 bits wide
  and and_3 (out_6, confirmar, comparador_out_3);
endmodule

module leds (
  input  A,
  input  B,
  input  C,
  input  D,
  output a_2,
  output b_2,
  output c_2,
  output d_2,
  output e,
  output f,
  output g
);

  wire and_1_out, and_2_out, and_3_out, and_4_out, and_5_out, and_6_out, and_7_out, and_8_out, and_9_out,
       and_10_out, and_11_out, and_12_out, and_13_out, and_14_out, and_15_out, and_16_out, and_17_out,
       and_18_out, and_19_out, and_20_out, and_21_out, and_22_out, and_23_out, and_24_out, and_25_out,
       and_26_out, and_27_out, and_28_out, and_29_out, and_30_out, and_31_out, and_32_out, and_33_out,
       and_34_out, and_35_out, not_1_out, not_2_out, not_3_out, not_4_out, not_5_out, not_6_out, not_7_out,
       not_8_out, not_9_out, not_10_out, not_11_out, not_12_out, not_13_out, not_14_out, not_15_out,
       not_16_out, not_17_out, not_18_out, not_19_out, not_20_out, not_21_out, not_22_out, not_23_out,
       not_24_out, not_25_out, not_26_out, not_27_out, not_28_out, not_29_out, not_30_out, not_31_out,
       not_32_out, not_33_out, not_34_out, not_35_out, not_36_out, not_37_out, not_38_out, not_39_out,
       not_40_out, not_41_out, not_42_out, not_43_out;

  not not_1 (not_1_out, B);
  and and_1 (and_1_out, not_1_out, not_2_out);
  not not_2 (not_2_out, D);
  not not_3 (not_3_out, A);
  and and_2 (and_2_out, not_3_out, C);
  not not_4 (not_4_out, A);
  and and_3 (and_3_out, not_4_out, B, D);
  and and_4 (and_4_out, B, C);
  not not_5 (not_5_out, B);
  and and_5 (and_5_out, A, not_5_out, not_6_out);
  not not_6 (not_6_out, C);
  and and_6 (and_6_out, A, not_7_out);
  not not_7 (not_7_out, D);
  not not_8 (not_8_out, A);
  and and_7 (and_7_out, not_8_out, not_9_out);
  not not_9 (not_9_out, B);
  not not_10 (not_10_out, A);
  and and_8 (and_8_out, not_10_out, not_11_out, not_12_out);
  not not_11 (not_11_out, C);
  not not_12 (not_12_out, D);
  not not_13 (not_13_out, B);
  and and_9 (and_9_out, not_13_out, not_14_out);
  not not_14 (not_14_out, D);
  not not_15 (not_15_out, A);
  and and_10 (and_10_out, not_15_out, C, D);
  and and_11 (and_11_out, A, not_16_out, D);
  not not_16 (not_16_out, C);
  not not_17 (not_17_out, A);
  and and_12 (and_12_out, not_17_out, not_18_out);
  not not_18 (not_18_out, C);
  not not_19 (not_19_out, A);
  and and_13 (and_13_out, not_19_out, D);
  not not_20 (not_20_out, C);
  and and_14 (and_14_out, not_20_out, D);
  not not_21 (not_21_out, A);
  and and_15 (and_15_out, not_21_out, B);
  and and_16 (and_16_out, A, not_22_out);
  not not_22 (not_22_out, B);
  not not_23 (not_23_out, A);
  and and_17 (and_17_out, not_23_out, not_24_out, not_25_out);
  not not_24 (not_24_out, B);
  not not_25 (not_25_out, D);
  not not_26 (not_26_out, B);
  and and_18 (and_18_out, not_26_out, C, D);
  and and_19 (and_19_out, B, not_27_out, D);
  not not_27 (not_27_out, C);
  and and_20 (and_20_out, B, C, not_28_out);
  not not_28 (not_28_out, D);
  and and_21 (and_21_out, A, not_29_out);
  not not_29 (not_29_out, C);
  not not_30 (not_30_out, B);
  and and_22 (and_22_out, not_30_out, not_31_out);
  not not_31 (not_31_out, D);
  and and_23 (and_23_out, C, not_32_out);
  not not_32 (not_32_out, D);
  and and_24 (and_24_out, A, C);
  and and_25 (and_25_out, A, B);
  not not_33 (not_33_out, C);
  and and_26 (and_26_out, not_33_out, not_34_out);
  not not_34 (not_34_out, D);
  not not_35 (not_35_out, A);
  and and_27 (and_27_out, not_35_out, B, not_36_out);
  not not_36 (not_36_out, C);
  and and_28 (and_28_out, B, not_37_out);
  not not_37 (not_37_out, D);
  and and_29 (and_29_out, A, not_38_out);
  not not_38 (not_38_out, B);
  and and_30 (and_30_out, A, C);
  not not_39 (not_39_out, B);
  and and_31 (and_31_out, not_39_out, C);
  and and_32 (and_32_out, C, not_40_out);
  not not_40 (not_40_out, D);
  not not_41 (not_41_out, A);
  and and_33 (and_33_out, not_41_out, B, not_42_out);
  not not_42 (not_42_out, C);
  and and_34 (and_34_out, A, not_43_out);
  not not_43 (not_43_out, B);
  and and_35 (and_35_out, A, D);
  or or_1 (b_2, and_7_out, and_8_out, and_9_out, and_10_out, and_11_out);
  or or_2 (c_2, and_12_out, and_13_out, and_14_out, and_15_out, and_16_out);
  or or_3 (d_2, and_17_out, and_18_out, and_19_out, and_20_out, and_21_out);
  or or_4 (e, and_22_out, and_23_out, and_24_out, and_25_out);
  or or_5 (f, and_26_out, and_27_out, and_28_out, and_29_out, and_30_out);
  or or_6 (g, and_31_out, and_32_out, and_33_out, and_34_out, and_35_out);
  or or_7 (a_2, and_1_out, and_2_out, and_3_out, and_4_out, and_5_out, and_6_out);
endmodule

module display (
  input  in_1,
  input  [3:0] in_2
);

  wire button_1_out, guess_1_out_6, leds_1_a_2, leds_1_b_2, leds_1_c_2, leds_1_d_2, leds_1_e, leds_1_f,
       leds_1_g;
  wire [7:0] rgbled_1_p1, rgbled_1_p2;

  Button button_1 (.out(button_1_out));
  LED led_1 (.in(guess_1_out_6));
  // RGBLed #(.multibit("true")) rgbled_1: pin names not known; wires that end beside it: rgbled_1_p1, rgbled_1_p2
  Guess guess_1 (
    .confirmar(in_1), .novo(button_1_out), .chute(in_2), .Red(rgbled_1_p1), .Blue(rgbled_1_p2),
    .out_6(guess_1_out_6));
  leds leds_1 (
    .A(in_2[3]), .B(in_2[2]), .C(in_2[1]), .D(in_2[0]), .a_2(leds_1_a_2), .b_2(leds_1_b_2), .c_2(leds_1_c_2),
    .d_2(leds_1_d_2), .e(leds_1_e), .f(leds_1_f), .g(leds_1_g));
  _7_Segment_Display u_7_segment_display_1 (
    .g(leds_1_g), .f(leds_1_f), .a(leds_1_a_2), .b(leds_1_b_2), .e(leds_1_e), .d(leds_1_d_2), .c(leds_1_c_2));  // open: dp
endmodule

module subtrator (
  input  x,
  input  y,
  input  b_in,
  output x___y,
  output b_out
);

  wire and_1_out, and_2_out, and_3_out, and_4_out, and_5_out, and_6_out, and_7_out;

  and and_1 (and_1_out, ~x, ~y, b_in);  // AND_Gate
  and and_2 (and_2_out, ~x, y, ~b_in);  // AND_Gate
  and and_3 (and_3_out, x, y, b_in);
  and and_4 (and_4_out, x, ~y, ~b_in);  // AND_Gate
  and and_5 (and_5_out, ~x, y);  // AND_Gate
  and and_6 (and_6_out, ~x, b_in);  // AND_Gate
  and and_7 (and_7_out, y, b_in);
  or or_1 (x___y, and_1_out, and_2_out, and_3_out, and_4_out);
  or or_2 (b_out, and_5_out, and_6_out, and_7_out);
endmodule

module subtrator_4 (
  input  [3:0] x,
  input  [3:0] y,
  output [3:0] out_3,
  output out_4
);

  wire subtrator_1_b_out, subtrator_1_x___y, subtrator_2_b_out, subtrator_2_x___y, subtrator_3_b_out,
       subtrator_3_x___y, subtrator_4_x___y;
  wire [1:0] bit_extender_1_out;
  wire [2:0] bit_extender_2_out;

  subtrator subtrator_1 (.x(x[0]), .y(y[0]), .b_in(1'b0), .x___y(subtrator_1_x___y), .b_out(subtrator_1_b_out));
  subtrator subtrator_2 (
    .x(x[1]), .y(y[1]), .b_in(subtrator_1_b_out), .x___y(subtrator_2_x___y), .b_out(subtrator_2_b_out));
  subtrator subtrator_3 (
    .x(x[2]), .y(y[2]), .b_in(subtrator_2_b_out), .x___y(subtrator_3_x___y), .b_out(subtrator_3_b_out));
  subtrator subtrator_4 (.x(x[3]), .y(y[3]), .b_in(subtrator_3_b_out), .x___y(subtrator_4_x___y), .b_out(out_4));
  assign bit_extender_1_out = {{1{subtrator_2_x___y}}, subtrator_1_x___y};  // Bit_Extender bit_extender_1
  assign bit_extender_2_out = {{1{subtrator_3_x___y}}, bit_extender_1_out};  // Bit_Extender bit_extender_2
  assign out_3 = {{1{subtrator_4_x___y}}, bit_extender_2_out};  // Bit_Extender bit_extender_3
endmodule

module \diferença  (
  input  [3:0] in_1,
  input  [3:0] in_2,
  output [3:0] out_3
);

  wire subtrator_4_2_out_4;
  wire [3:0] subtrator_4_1_out_3, subtrator_4_2_out_3;

  subtrator_4 subtrator_4_1 (.x(in_2), .y(in_1), .out_3(subtrator_4_1_out_3));  // open: out_4
  subtrator_4 subtrator_4_2 (.x(in_1), .y(in_2), .out_3(subtrator_4_2_out_3), .out_4(subtrator_4_2_out_4));
  Multiplexer #(.width(4), .enable("false")) multiplexer_1 (
    .in0(subtrator_4_1_out_3), .in1(subtrator_4_2_out_3), .out(out_3), .sel(subtrator_4_2_out_4));
endmodule

module leftshift_4 (
  input  [3:0] in_1,
  output [7:0] out_2
);

  wire [4:0] bit_extender_1_out;
  wire [5:0] bit_extender_3_out;
  wire [6:0] bit_extender_2_out;

  assign bit_extender_1_out = {{1{in_1[0]}}, 4'b0000};  // Bit_Extender bit_extender_1
  assign bit_extender_2_out = {{1{in_1[2]}}, bit_extender_3_out};  // Bit_Extender bit_extender_2
  assign bit_extender_3_out = {{1{in_1[1]}}, bit_extender_1_out};  // Bit_Extender bit_extender_3
  assign out_2 = {{1{in_1[3]}}, bit_extender_2_out};  // Bit_Extender bit_extender_4
endmodule
